# Fritzing sketch BreakInMotor (saved by Fritzing 0.9.3b)
breadboards: 1

parts:
  U1 = TA7291P [package=HSIP10-P-2.54(THT)]
  VCC2 = Battery
  パーツ1 = Arduino Pro Mini (5V)
  VCC1 = Battery
  VCC3 = Battery
  M1 = DC Motor
  Grove1 = Grove OLED 128x96
  SERVO1 = Tower Pro SG90 servo [part_number=101246]
  S1 = Toggle Switch [package=THT]

nets:
  GND: U1.GND, VCC2.-, パーツ1.GND, VCC3.-, Grove1.GND, SERVO1.GND
  N1: U1.OUT1, M1.pin_2
  N2: U1.IN1, パーツ1.D8
  N3: U1.IN2, パーツ1.D9
  VCC: U1.Vcc, パーツ1.VCC, Grove1.VCC, SERVO1.+5V, S1.COM
  N4: U1.Vs, VCC3.+
  N5: U1.OUT2, M1.pin_1
  N6: VCC2.+, VCC1.-
  N7: パーツ1.A6, Grove1.SCL
  N8: パーツ1.A7, Grove1.SDA
  N9: パーツ1.D10, SERVO1.Signal
  N10: VCC1.+, S1.L1

custom parts:
  TA7291P: The IC are Full-Bridge Driver. 4 modes available (CW / CCW / STOP / BRAKE) and PWM control. Output current:1.0 A (AVE.) 2.0 A (PEAK)
  Tower Pro SG90 servo: Original file by John De Cristofaro http://www.adafruit.com/products/1449 Adafruit Feedback Servo (Small) Edited by: e-radionica.com 28/9/2015
