# Fritzing sketch RPi_2_Arduino (saved by Fritzing 0.9.2b)
breadboards: 1

parts:
  Raspberry_Pi1 = Raspberry Pi 2
  パーツ1 = Arduino Pro Mini v13
  パーツ2 = Logic Level Converter

nets:
  3V3: Raspberry_Pi1.3v3, Raspberry_Pi1.3V3, パーツ2.LV
  GND: Raspberry_Pi1.GND, パーツ1.GND, パーツ2.GND
  N1: Raspberry_Pi1.GPIO15, パーツ2.RX_LV
  N2: Raspberry_Pi1.GPIO14, パーツ2.TX_LV
  5V: Raspberry_Pi1.5V, パーツ1.VCC, パーツ2.HV
  N3: パーツ1.D1/RX, パーツ2.TX_HV
  N4: パーツ1.D0/TX, パーツ2.RX_HV
