# Fritzing sketch RPi_CtrlDCMotor (saved by Fritzing 0.9.2b)
breadboards: 1

parts:
  Raspberry_Pi1 = Raspberry Pi 2
  R1 = Resistor [tolerance=±5% resistance=10k package=THT]
  LED1 = LED - 5mm [color="Red (633nm)" package="5 mm [THT]"]
  M1 = DC Motor
  BATT1 = 3xAAA Switchable Battery Pack w/Bare Wire
  Q1 = TRANSISTOR_NPN [package=to-92]
  R2 = Resistor [tolerance=±5% resistance=10k package=THT]
  LED2 = LED - 5mm [color="Red (633nm)" package="5 mm [THT]"]

nets:
  N1: Raspberry_Pi1.GND, BATT1.NEG, R2.Pin_1
  N2: Raspberry_Pi1.GPIO17, R1.Pin_0
  N3: R1.Pin_1, LED1.anode
  N4: LED1.cathode, Q1.B
  N5: M1.pin_1, BATT1.POS, LED2.cathode
  N6: M1.pin_2, Q1.C, LED2.anode
  N7: Q1.E, R2.Pin_0

custom parts:
  3xAAA Switchable Battery Pack w/Bare Wire: 3xAAA Switchable Battery Pack w/Bare Wire Connectors
