# Fritzing sketch RPi_CtrlDualServo (saved by Fritzing 0.9.2b)

parts:
  Raspberry_Pi1 = Raspberry Pi 2
  J1 = Basic Servo
  J2 = Basic Servo

nets:
  GND: Raspberry_Pi1.GND, J1.gnd, J2.gnd
  N1: Raspberry_Pi1.GPIO13, J2.pulse
  N2: Raspberry_Pi1.GPIO12, J1.pulse
  VCC: Raspberry_Pi1.5V, J1.vcc, J2.vcc
