# Fritzing sketch RPi_ReadGPIO (saved by Fritzing 0.9.2b)
breadboards: 1

parts:
  Raspberry_Pi1 = Raspberry Pi 2
  R1 = Resistor [tolerance=±5% resistance=10k package=THT]
  LED1 = LED - 5mm [color="Red (633nm)" package="5 mm [THT]"]
  R2 = Resistor [tolerance=±5% resistance=10k package=THT]
  S1 = Pushbutton [package="[THT]"]

nets:
  3V3: Raspberry_Pi1.3v3, Raspberry_Pi1.3V3, S1.Pin_1, S1.Pin_2
  N1: Raspberry_Pi1.GND, LED1.cathode, R2.Pin_1
  N2: Raspberry_Pi1.GPIO17, R1.Pin_0
  N3: Raspberry_Pi1.GPIO18, R2.Pin_0, S1.Pin_3, S1.Pin_4
  N4: R1.Pin_1, LED1.anode
