# Fritzing sketch RPi_XBee_Arduino (saved by Fritzing 0.9.2b)
breadboards: 2

parts:
  Raspberry_Pi1 = Raspberry Pi 2
  U1 = XBee
  U2 = XBee
  パーツ1 = Logic Level Converter
  パーツ2 = Arduino Pro Mini v13

nets:
  3V3: Raspberry_Pi1.3v3, U1.VCC
  N1: Raspberry_Pi1.GPIO15, U1.pin2
  N2: Raspberry_Pi1.GPIO14, U1.pin3
  GND: Raspberry_Pi1.GND, U1.GND
  N3: U2.VCC, パーツ1.LV
  N4: U2.pin2, パーツ1.TX_LV
  N5: U2.pin3, パーツ1.RX_LV
  GND_2: U2.GND, パーツ1.GND, パーツ2.GND
  N6: パーツ1.TX_HV, パーツ2.D1/RX
  N7: パーツ1.RX_HV, パーツ2.D0/TX
  N8: パーツ1.HV, パーツ2.VCC
